# Fritzing sketch RTKBaseStation (saved by Fritzing 0.9.9b)
breadboards: 1

parts:
  Part1 = Adafruit HUZZAH32 ESP32 Feather [part_number="Adafruit #3405"]
  Qwiic1_RTK-SMA = Qwiic Connector  # not connected
  10_k = Resistor [tolerance=±5% power=0.25 resistance=220 package=THT]
  Wipe = Pushbutton [package="[SMD]"]
  BAT1 = Battery Holders [package=lipo-1100mAh]
  Qwiic2_Oled_Display_on_RTK2 = Qwiic Connector  # not connected
  Reset = Pushbutton [package="[SMD]"]

nets:
  N1: Part1.GND, 10_k.Pin_1, BAT1.-, Reset.Pin_3, Reset.Pin_4
  N2: Part1.3.3V, Wipe.Pin_1, Wipe.Pin_2
  N3: Part1.RESET, Reset.Pin_1, Reset.Pin_2
  N4: Part1.VBAT, BAT1.+
  N5: Part1.IO15_A8, 10_k.Pin_0, Wipe.Pin_3, Wipe.Pin_4

custom parts:
  Qwiic Connector: Qwiic PCB connector
